// Digital circuit CPU 16.dig as structural Verilog
module CPU_16 (
  input  Clock,
  input  nWAIT,
  output CLK1,
  output CLK2
);

  wire _74245_1_p13, _74245_1_p14, _74245_1_p15, _74245_1_p16, _74245_1_p17, _74245_1_p18, _74245_1_p19,
       _74245_1_p20, _74245_2_p13, _74245_2_p14, _74245_2_p15, _74245_2_p16, _74245_2_p17, _74245_2_p18,
       _74245_2_p19, _74245_2_p20, _74245_3_p13, _74245_3_p14, _74245_3_p15, _74245_3_p16, _74245_3_p17,
       _74245_3_p18, _74245_3_p19, _74245_3_p20, _74245_4_p13, _74245_4_p14, _74245_4_p15, _74245_4_p16,
       _74245_4_p17, _74245_4_p18, _74245_4_p19, _74245_4_p20, and_1_out, and_2_out, and_3_out, and_4_out,
       and_5_out, and_6_out, and_7_out, and_10_out, and_11_out, bussplitter_1_d0, bussplitter_1_d1,
       bussplitter_1_d2, bussplitter_1_d3, bussplitter_1_d4, bussplitter_1_d5, bussplitter_1_d6,
       bussplitter_1_d7, bussplitter_1_d8, bussplitter_1_d9, bussplitter_1_d10, bussplitter_1_d11,
       bussplitter_1_d12, bussplitter_1_d13, bussplitter_1_d14, bussplitter_1_d15, bussplitter_3_d0,
       bussplitter_3_d1, bussplitter_3_d2, bussplitter_3_d3, bussplitter_3_d4, bussplitter_3_d5,
       bussplitter_3_d6, bussplitter_3_d7, bussplitter_3_d8, bussplitter_3_d9, bussplitter_3_d10,
       bussplitter_3_d11, bussplitter_3_d12, bussplitter_3_d13, bussplitter_3_d14, bussplitter_3_d15, COND_C,
       COND_N, COND_NEG, COND_RES, COND_Z, CONV_V, demultiplexer_1_out_0, demultiplexer_1_out_1,
       demultiplexer_2_out_1, demultiplexer_2_out_2, demultiplexer_2_out_3, demultiplexer_3_out_1,
       demultiplexer_3_out_2, demultiplexer_3_out_3, demultiplexer_3_out_4, demultiplexer_4_out_1,
       demultiplexer_4_out_2, demultiplexer_4_out_3, demultiplexer_4_out_4, demultiplexer_4_out_5,
       demultiplexer_4_out_6, demultiplexer_4_out_7, demultiplexer_5_out_0, demultiplexer_6_out_0,
       demultiplexer_6_out_1, demultiplexer_7_out_1, demultiplexer_7_out_2, demultiplexer_7_out_3,
       demultiplexer_7_out_4, demultiplexer_7_out_5, demultiplexer_7_out_6, demultiplexer_7_out_7,
       demultiplexer_8_out_0, demultiplexer_8_out_1, demultiplexer_8_out_2, demultiplexer_8_out_3,
       demultiplexer_9_out_0, demultiplexer_9_out_1, demultiplexer_9_out_2, demultiplexer_9_out_3,
       demultiplexer_9_out_4, demultiplexer_9_out_5, demultiplexer_9_out_6, demultiplexer_9_out_7,
       demultiplexer_10_out_0, demultiplexer_10_out_1, demultiplexer_10_out_2, demultiplexer_10_out_3,
       demultiplexer_10_out_4, demultiplexer_10_out_5, demultiplexer_10_out_6, demultiplexer_10_out_7,
       FAULT_VECT_any, FLAG_C, FLAG_V, HLT, HLT_ack, IRQ_0, IRQ_ack, IRQ_VECT_any, keyboard_1_av, MEM_dir,
       nF_ALUin, nF_DATin, nF_DATout, nF_st, nIR_st, nIRQ_en, nMAR_ADSout, nMAR_st, nMASK_Fst, nMDR_DATout,
       nMDR_st, nMEM_DATout, nMEM_en, nMEM_st, nMSK_st, nOP1_st, nOP2_st, nor_1_out, nor_2_out, nor_3_out,
       nor_4_out, nor_5_out, nor_6_out, nor_7_out, nor_8_out, not_14_out, not_15_out, not_16_out, not_28_out,
       not_29_out, not_30_out, not_31_out, not_32_out, not_33_out, not_34_out, not_35_out, not_36_out,
       not_37_out, not_38_out, not_39_out, not_40_out, not_41_out, not_42_out, not_44_out, not_45_out,
       not_51_out, not_52_out, not_53_out, not_54_out, not_55_out, not_56_out, not_66_out, not_67_out,
       not_68_out, not_69_out, nPAN_HLTen, nPC_ADSout, nPC_DATout, nPC_en, nPC_st, nREG_DATout, nREG_st,
       nRSH_DATout, nRST, nRST_SEQen, nSEQ_en, nSEQ_st, nSEX_DATout, nSP_ADSout, nSP_DATout, nSP_en, nSP_st,
       nSUM_DATout, nSWP_DATout, nWRD_DATout, or_3_out, or_4_out, or_5_out, or_7_out, or_8_out, REG_aop,
       REG_dir, RESET_out, RST_ack, RST_IRen, RUN_out, SEQ_val, SP_dir, STP, t_ff_1_nq, t_ff_1_q, TMP_clr,
       \Σ_Csel , \Σ_Cval , \Σ_M ;
  wire [2:0] AOUT_sel, COND_sel, REG_ADS;
  wire [3:0] alu_1_c_f, DOUT_sel, driverinvsel_3_out, FLAGS, ST_sel, \µSEQ_out , \Σ_sel ;
  wire [5:4] HLT_q;
  wire [6:0] MASK_q;
  wire [10:4] undriven;
  wire [15:0] _15_out, ADDRESS, alu_1_sum, barrelshifter_1_out, bitextender_1_out, d_ff_1_q, d_ff_2_q, DATA,
       driverinvsel_2_out, IR_q, MAR_q, MDR_q, MEMDATA, OP1_q, OP2_out, PC_out, REGS__16x8_d, SP_out;
  wire [47:0] \µCODE_d ;
  wire [47:21] CTRL_q;

  Demultiplexer demultiplexer_1 (
    .sel(ST_sel[3]), .in(1'b1), .out_0(demultiplexer_1_out_0), .out_1(demultiplexer_1_out_1));
  Demultiplexer #(.Selector_Bits(3)) demultiplexer_2 (
    .sel(AOUT_sel), .in(1'b1), .out_1(demultiplexer_2_out_1), .out_2(demultiplexer_2_out_2),
    .out_3(demultiplexer_2_out_3));  // open: out_0, out_4, out_5, out_6, out_7
  Demultiplexer #(.Selector_Bits(3)) demultiplexer_3 (
    .sel(COND_sel), .in(1'b1), .out_1(demultiplexer_3_out_1), .out_2(demultiplexer_3_out_2),
    .out_3(demultiplexer_3_out_3), .out_4(demultiplexer_3_out_4));  // open: out_0, out_5, out_6, out_7
  Demultiplexer #(.Selector_Bits(3)) demultiplexer_4 (
    .sel(ST_sel[2:0]), .in(demultiplexer_1_out_0), .out_1(demultiplexer_4_out_1),
    .out_2(demultiplexer_4_out_2), .out_3(demultiplexer_4_out_3), .out_4(demultiplexer_4_out_4),
    .out_5(demultiplexer_4_out_5), .out_6(demultiplexer_4_out_6), .out_7(demultiplexer_4_out_7));  // open: out_0
  Demultiplexer #(.Selector_Bits(3)) demultiplexer_5 (
    .sel(ST_sel[2:0]), .in(demultiplexer_1_out_1), .out_0(demultiplexer_5_out_0));  // open: out_1, out_2, out_3, out_4, out_5, out_6, out_7
  not not_1 (nSP_ADSout, demultiplexer_2_out_1);
  not not_2 (nPC_ADSout, demultiplexer_2_out_2);
  not not_3 (nMAR_ADSout, demultiplexer_2_out_3);
  not not_4 (COND_N, demultiplexer_3_out_1);
  not not_5 (COND_Z, demultiplexer_3_out_2);
  not not_6 (CONV_V, demultiplexer_3_out_3);
  not not_7 (COND_C, demultiplexer_3_out_4);
  not not_8 (nSP_st, demultiplexer_4_out_1);
  not not_9 (nPC_st, demultiplexer_4_out_2);
  not not_10 (nOP1_st, demultiplexer_4_out_3);
  not not_11 (nOP2_st, demultiplexer_4_out_4);
  not not_12 (nIR_st, demultiplexer_4_out_5);
  not not_13 (nMDR_st, demultiplexer_4_out_6);
  not not_14 (not_14_out, demultiplexer_4_out_7);
  not not_15 (not_15_out, demultiplexer_5_out_0);
  Register #(.Bits(7)) MASK (.D(DATA[10:4]), .C(CLK2), .en(~nMASK_Fst), .Q(MASK_q));
  or or_1 (nMEM_st, ~CLK2, not_14_out);  // Or
  or or_2 (nREG_st, ~CLK2, not_15_out);  // Or
  and and_1 (and_1_out, ~COND_N, FLAGS[0]);  // And
  and and_2 (and_2_out, ~COND_Z, FLAGS[1]);  // And
  and and_3 (and_3_out, ~CONV_V, FLAGS[2]);  // And
  not not_16 (not_16_out, IRQ_0);
  nor nor_1 (nor_1_out, MASK_q[0], 1'b1);
  nor nor_2 (nor_2_out, MASK_q[1], 1'b1);
  nor nor_3 (nor_3_out, MASK_q[2], 1'b1);
  nor nor_4 (nor_4_out, MASK_q[3], 1'b1);
  nor nor_5 (nor_5_out, MASK_q[4], 1'b1);
  nor nor_6 (nor_6_out, MASK_q[5], 1'b1);
  nor nor_7 (nor_7_out, MASK_q[6], 1'b1);
  or or_3 (or_3_out, and_1_out, and_2_out);
  and and_4 (and_4_out, ~COND_C, ~FLAGS[3]);  // And
  Demultiplexer demultiplexer_6 (
    .sel(DOUT_sel[3]), .in(1'b1), .out_0(demultiplexer_6_out_0), .out_1(demultiplexer_6_out_1));
  Demultiplexer #(.Selector_Bits(3)) demultiplexer_7 (
    .sel(DOUT_sel[2:0]), .in(demultiplexer_6_out_0), .out_1(demultiplexer_7_out_1),
    .out_2(demultiplexer_7_out_2), .out_3(demultiplexer_7_out_3), .out_4(demultiplexer_7_out_4),
    .out_5(demultiplexer_7_out_5), .out_6(demultiplexer_7_out_6), .out_7(demultiplexer_7_out_7));  // open: out_0
  Demultiplexer #(.Selector_Bits(3)) demultiplexer_8 (
    .sel(DOUT_sel[2:0]), .in(demultiplexer_6_out_1), .out_0(demultiplexer_8_out_0),
    .out_1(demultiplexer_8_out_1), .out_2(demultiplexer_8_out_2), .out_3(demultiplexer_8_out_3));  // open: out_4, out_5, out_6, out_7
  or or_4 (or_4_out, and_3_out, and_4_out);
  not not_17 (nF_DATout, demultiplexer_7_out_1);
  not not_18 (nSP_DATout, demultiplexer_7_out_2);
  not not_19 (nPC_DATout, demultiplexer_7_out_3);
  not not_20 (nSUM_DATout, demultiplexer_7_out_4);
  not not_21 (nRSH_DATout, demultiplexer_7_out_5);
  not not_22 (nSEX_DATout, demultiplexer_7_out_6);
  not not_23 (nSWP_DATout, demultiplexer_7_out_7);
  not not_24 (nWRD_DATout, demultiplexer_8_out_0);
  not not_25 (nMDR_DATout, demultiplexer_8_out_1);
  not not_26 (nMEM_DATout, demultiplexer_8_out_2);
  not not_27 (nREG_DATout, demultiplexer_8_out_3);
  PriorityEncoder #(.Selector_Bits(3)) IRQ_VECT (
    .in0(not_16_out), .in1(nor_1_out), .in2(nor_2_out), .in3(nor_3_out), .in4(nor_4_out), .in5(nor_5_out),
    .in6(nor_6_out), .in7(nor_7_out), .any(IRQ_VECT_any));  // open: num
  PriorityEncoder #(.Selector_Bits(3)) FAULT_VECT (.any(FAULT_VECT_any));  // open: in0, in1, in2, in3, in4, in5, in6, in7, num
  or or_5 (or_5_out, or_3_out, or_4_out);
  not not_28 (not_28_out, IRQ_VECT_any);
  not not_29 (not_29_out, FAULT_VECT_any);
  not not_30 (not_30_out, or_5_out);
  Demultiplexer #(.Selector_Bits(3)) demultiplexer_9 (
    .sel(ADDRESS[15:13]), .in(not_31_out), .out_0(demultiplexer_9_out_0), .out_1(demultiplexer_9_out_1),
    .out_2(demultiplexer_9_out_2), .out_3(demultiplexer_9_out_3), .out_4(demultiplexer_9_out_4),
    .out_5(demultiplexer_9_out_5), .out_6(demultiplexer_9_out_6), .out_7(demultiplexer_9_out_7));
  not not_31 (not_31_out, nMEM_en);
  Demultiplexer #(.Selector_Bits(3)) demultiplexer_10 (
    .sel(ADDRESS[6:4]), .in(not_32_out), .out_0(demultiplexer_10_out_0), .out_1(demultiplexer_10_out_1),
    .out_2(demultiplexer_10_out_2), .out_3(demultiplexer_10_out_3), .out_4(demultiplexer_10_out_4),
    .out_5(demultiplexer_10_out_5), .out_6(demultiplexer_10_out_6), .out_7(demultiplexer_10_out_7));
  not not_32 (not_32_out, not_40_out);
  not not_33 (not_33_out, COND_RES);
  Multiplexer multiplexer_1 (.sel(COND_NEG), .in_0(or_5_out), .in_1(not_30_out), .out(COND_RES));
  not not_34 (not_34_out, demultiplexer_9_out_0);
  not not_35 (not_35_out, demultiplexer_9_out_1);
  not not_36 (not_36_out, demultiplexer_9_out_2);
  not not_37 (not_37_out, demultiplexer_9_out_3);
  not not_38 (not_38_out, demultiplexer_9_out_4);
  not not_39 (not_39_out, demultiplexer_9_out_5);
  not not_40 (not_40_out, demultiplexer_9_out_6);
  not not_41 (not_41_out, demultiplexer_9_out_7);
  not not_42 (not_42_out, demultiplexer_10_out_0);
  // Not not_43 has open pins: in=demultiplexer_10_out_1, out=open
  not not_44 (not_44_out, demultiplexer_10_out_2);
  not not_45 (not_45_out, demultiplexer_10_out_3);
  // Not not_46 has open pins: in=demultiplexer_10_out_4, out=open
  // Not not_47 has open pins: in=demultiplexer_10_out_5, out=open
  // Not not_48 has open pins: in=demultiplexer_10_out_6, out=open
  // Not not_49 has open pins: in=demultiplexer_10_out_7, out=open
  not not_50 (nRST, RESET_out);
  DipSwitch RESET (.out(RESET_out));
  and and_5 (and_5_out, nSEQ_en, nRST_SEQen);
  and and_6 (and_6_out, nSEQ_st, not_33_out);
  PullUp pullup_1 (.out(HLT));
  assign DATA = ~nWRD_DATout ? {16{1'b1}} : 16'bz;  // DriverInvSel driverinvsel_1
  or or_6 (nMSK_st, nMEM_st, not_42_out);
  PullDown pulldown_1 (.out(Clock));
  nor nor_8 (nor_8_out, HLT, RST_IRen);
  and and_7 (and_7_out, not_28_out, not_29_out);
  or or_7 (or_7_out, not_34_out, not_35_out, not_36_out, not_37_out, not_38_out, not_39_out);
  not not_51 (not_51_out, not_44_out);
  not not_52 (not_52_out, not_45_out);
  T_FF #(.withEnable("false")) t_ff_1 (.C(not_53_out), .Q(t_ff_1_q), .nQ(t_ff_1_nq));
  not not_53 (not_53_out, Clock);
  not not_54 (not_54_out, TMP_clr);
  not not_55 (not_55_out, RST_ack);
  assign driverinvsel_2_out = ~RST_IRen ? DATA : 16'bz;  // DriverInvSel driverinvsel_2
  PullDown #(.Bits(16)) pulldown_2 (.out(DATA));
  Terminal terminal_1 (.D(DATA[7:0]), .C(CLK2), .en(not_51_out));
  Keyboard keyboard_1 (.C(CLK2), .en(not_52_out), .D(MEMDATA), .av(keyboard_1_av));
  // _7474 _7474_1: pin names not known; wires that end beside it: nRST, 1'b0, 1'b0, not_54_out, nRST, 1'b0, 1'b0, not_55_out, 1'b1, 1'b0, nRST_SEQen, RST_IRen
  CounterPreset #(.Bits(4)) \u_µSEQ  (
    .en(~and_5_out), .C(CLK2), .dir(1'b0), .in({3'b000, SEQ_val}), .ld(~and_6_out), .clr(1'b0),
    .out(\µSEQ_out ));  // open: ovf
  Register u_HLT (.D(nor_8_out), .C(CLK2), .en(~1'b0), .Q(HLT_q[4]));
  Register IRQ (.D(and_7_out), .C(CLK2), .en(~nIRQ_en), .Q(HLT_q[5]));
  PullDown #(.Bits(16)) pulldown_3 (.out(driverinvsel_2_out));
  Register #(.Bits(16)) IR (.D(driverinvsel_2_out), .C(CLK2), .en(~nIR_st), .Q(IR_q));
  ROM #(.AddrBits(16), .Bits(16)) ROM_16x64k (.A(ADDRESS), .sel(not_56_out), .D(MEMDATA));
  not not_56 (not_56_out, not_41_out);
  RAMSinglePortSel #(.AddrBits(16), .Bits(16)) RAM0_16x64k (
    .A(ADDRESS), .CS(~or_7_out), .WE(~nMEM_st), .OE(~nMEM_DATout), .D(MEMDATA));
  not not_57 (IRQ_0, keyboard_1_av);
  and and_8 (CLK1, Clock, t_ff_1_q);
  and and_9 (CLK2, t_ff_1_nq, ~nWAIT, Clock);  // And
  BusSplitter #(.Bits(16)) bussplitter_1 (
    .D(MEMDATA), .OE(MEM_dir), .D0(bussplitter_1_d0), .D1(bussplitter_1_d1), .D2(bussplitter_1_d2),
    .D3(bussplitter_1_d3), .D4(bussplitter_1_d4), .D5(bussplitter_1_d5), .D6(bussplitter_1_d6),
    .D7(bussplitter_1_d7), .D8(bussplitter_1_d8), .D9(bussplitter_1_d9), .D10(bussplitter_1_d10),
    .D11(bussplitter_1_d11), .D12(bussplitter_1_d12), .D13(bussplitter_1_d13), .D14(bussplitter_1_d14),
    .D15(bussplitter_1_d15));
  PullDown #(.Bits(16)) pulldown_4 (.out(MEMDATA));
  Multiplexer #(.Bits(3)) multiplexer_2 (.sel(REG_aop), .in_0(IR_q[2:0]), .in_1(IR_q[5:3]), .out(REG_ADS));
  PullDown pulldown_5 (.out(bussplitter_1_d0));
  PullDown pulldown_6 (.out(bussplitter_1_d1));
  PullDown pulldown_7 (.out(bussplitter_1_d2));
  PullDown pulldown_8 (.out(bussplitter_1_d15));
  PullDown pulldown_9 (.out(bussplitter_1_d14));
  PullDown pulldown_10 (.out(bussplitter_1_d13));
  ROM #(.AddrBits(16), .Bits(48)) \u_µCODE  (.A({IR_q[15:6], HLT_q, \µSEQ_out }), .sel(1'b1), .D(\µCODE_d ));
  PullDown pulldown_11 (.out(bussplitter_1_d3));
  PullDown pulldown_12 (.out(bussplitter_1_d4));
  PullDown pulldown_13 (.out(bussplitter_1_d5));
  PullDown pulldown_14 (.out(bussplitter_1_d6));
  PullDown pulldown_15 (.out(bussplitter_1_d12));
  PullDown pulldown_16 (.out(bussplitter_1_d11));
  PullDown pulldown_17 (.out(bussplitter_1_d10));
  PullDown pulldown_18 (.out(bussplitter_1_d9));
  PullDown pulldown_19 (.out(bussplitter_1_d7));
  PullDown pulldown_20 (.out(bussplitter_1_d8));
  D_FF #(.Bits(48)) CTRL (
    .D(\µCODE_d ), .C(CLK1),
    .Q({CTRL_q[47:38], RST_ack, IRQ_ack, HLT_ack, TMP_clr, REG_aop, REG_dir, CTRL_q[31], nF_ALUin, COND_NEG, MEM_dir, CTRL_q[27:26], SP_dir, CTRL_q[24], SEQ_val, CTRL_q[22:21], \Σ_Cval , \Σ_Csel , \Σ_M , \Σ_sel , COND_sel, AOUT_sel, DOUT_sel, ST_sel}));  // open: nQ
  // _74245 _74245_1: pin names not known; wires that end beside it: MEM_dir, 1'b1, 1'b0, bussplitter_1_d0, bussplitter_1_d1, bussplitter_1_d2, bussplitter_1_d3, bussplitter_1_d4, bussplitter_1_d5, bussplitter_1_d6, bussplitter_1_d7, 1'b0, _74245_1_p13, _74245_1_p14, _74245_1_p15, _74245_1_p16, _74245_1_p17, _74245_1_p18, _74245_1_p19, _74245_1_p20
  // _74245 _74245_2: pin names not known; wires that end beside it: MEM_dir, 1'b1, 1'b0, bussplitter_1_d8, bussplitter_1_d9, bussplitter_1_d10, bussplitter_1_d11, bussplitter_1_d12, bussplitter_1_d13, bussplitter_1_d14, bussplitter_1_d15, 1'b0, _74245_2_p13, _74245_2_p14, _74245_2_p15, _74245_2_p16, _74245_2_p17, _74245_2_p18, _74245_2_p19, _74245_2_p20
  not not_58 (nSEQ_en, CTRL_q[21]);
  not not_59 (nSEQ_st, CTRL_q[22]);
  not not_60 (nPC_en, CTRL_q[24]);
  not not_61 (nSP_en, CTRL_q[26]);
  not not_62 (nMEM_en, CTRL_q[27]);
  not not_63 (nIRQ_en, CTRL_q[31]);
  not not_64 (nMAR_st, CTRL_q[38]);
  PullDown pulldown_21 (.out(_74245_2_p20));
  PullDown pulldown_22 (.out(_74245_2_p19));
  PullDown pulldown_23 (.out(_74245_2_p18));
  not not_65 (nF_DATin, nF_ALUin);
  PullDown pulldown_24 (.out(_74245_2_p17));
  PullDown pulldown_25 (.out(_74245_2_p16));
  PullDown pulldown_26 (.out(_74245_2_p15));
  PullDown pulldown_27 (.out(_74245_2_p14));
  PullDown pulldown_28 (.out(_74245_2_p13));
  PullDown pulldown_29 (.out(_74245_1_p20));
  PullDown pulldown_30 (.out(_74245_1_p19));
  PullDown pulldown_31 (.out(_74245_1_p18));
  PullDown pulldown_32 (.out(_74245_1_p17));
  PullDown pulldown_33 (.out(_74245_1_p16));
  PullDown pulldown_34 (.out(_74245_1_p15));
  PullDown pulldown_35 (.out(_74245_1_p14));
  not not_66 (not_66_out, MEM_dir);
  BusSplitter #(.Bits(16)) bussplitter_2 (
    .D(DATA), .OE(not_66_out), .D0(_74245_1_p13), .D1(_74245_1_p14), .D2(_74245_1_p15), .D3(_74245_1_p16),
    .D4(_74245_1_p17), .D5(_74245_1_p18), .D6(_74245_1_p19), .D7(_74245_1_p20), .D8(_74245_2_p13),
    .D9(_74245_2_p14), .D10(_74245_2_p15), .D11(_74245_2_p16), .D12(_74245_2_p17), .D13(_74245_2_p18),
    .D14(_74245_2_p19), .D15(_74245_2_p20));
  PullDown pulldown_36 (.out(_74245_1_p13));
  LED D15 (.in(d_ff_1_q[15]));
  LED A15 (.in(d_ff_2_q[15]));
  DipSwitch _15 (.out(_15_out[15]));
  or or_8 (or_8_out, CLK2, TMP_clr);
  RAMSinglePortSel #(.AddrBits(3), .Bits(16)) REGS__16x8 (
    .A(REG_ADS), .CS(~1'b0), .WE(~nREG_st), .OE(~nREG_DATout), .D(REGS__16x8_d));
  LED D13 (.in(d_ff_1_q[13]));
  LED D14 (.in(d_ff_1_q[14]));
  LED A13 (.in(d_ff_2_q[13]));
  LED A14 (.in(d_ff_2_q[14]));
  DipSwitch _13 (.out(_15_out[13]));
  DipSwitch _14 (.out(_15_out[14]));
  Register #(.Bits(16)) OP1 (.D(DATA), .C(CLK2), .en(~nOP1_st), .Q(OP1_q));
  CounterPreset #(.Bits(16)) OP2 (
    .en(~1'b1), .C(or_8_out), .dir(1'b0), .in(DATA), .ld(~nOP2_st), .clr(TMP_clr), .out(OP2_out));  // open: ovf
  LED D12 (.in(d_ff_1_q[12]));
  LED A12 (.in(d_ff_2_q[12]));
  DipSwitch _12 (.out(_15_out[12]));
  BusSplitter #(.Bits(16)) bussplitter_3 (
    .D(REGS__16x8_d), .OE(REG_dir), .D0(bussplitter_3_d0), .D1(bussplitter_3_d1), .D2(bussplitter_3_d2),
    .D3(bussplitter_3_d3), .D4(bussplitter_3_d4), .D5(bussplitter_3_d5), .D6(bussplitter_3_d6),
    .D7(bussplitter_3_d7), .D8(bussplitter_3_d8), .D9(bussplitter_3_d9), .D10(bussplitter_3_d10),
    .D11(bussplitter_3_d11), .D12(bussplitter_3_d12), .D13(bussplitter_3_d13), .D14(bussplitter_3_d14),
    .D15(bussplitter_3_d15));
  PullDown #(.Bits(16)) pulldown_37 (.out(REGS__16x8_d));
  LED D11 (.in(d_ff_1_q[11]));
  LED A11 (.in(d_ff_2_q[11]));
  DipSwitch _11 (.out(_15_out[11]));
  PullDown pulldown_38 (.out(bussplitter_3_d0));
  PullDown pulldown_39 (.out(bussplitter_3_d1));
  PullDown pulldown_40 (.out(bussplitter_3_d2));
  PullDown pulldown_41 (.out(bussplitter_3_d15));
  PullDown pulldown_42 (.out(bussplitter_3_d14));
  PullDown pulldown_43 (.out(bussplitter_3_d13));
  LED D9 (.in(d_ff_1_q[9]));
  LED D10 (.in(d_ff_1_q[10]));
  LED A9 (.in(d_ff_2_q[9]));
  LED A10 (.in(d_ff_2_q[10]));
  DipSwitch _9 (.out(_15_out[9]));
  DipSwitch _10 (.out(_15_out[10]));
  PullDown pulldown_44 (.out(bussplitter_3_d3));
  PullDown pulldown_45 (.out(bussplitter_3_d4));
  PullDown pulldown_46 (.out(bussplitter_3_d5));
  PullDown pulldown_47 (.out(bussplitter_3_d6));
  PullDown pulldown_48 (.out(bussplitter_3_d12));
  PullDown pulldown_49 (.out(bussplitter_3_d11));
  PullDown pulldown_50 (.out(bussplitter_3_d10));
  PullDown pulldown_51 (.out(bussplitter_3_d9));
  LED D8 (.in(d_ff_1_q[8]));
  LED A8 (.in(d_ff_2_q[8]));
  DipSwitch _8 (.out(_15_out[8]));
  BarrelShifter #(.Bits(16), .direction("right")) barrelshifter_1 (
    .in(OP1_q), .shift(5'b00001), .out(barrelshifter_1_out));
  BitExtender bitextender_1 (.in(OP1_q[7:0]), .out(bitextender_1_out));
  PullDown pulldown_52 (.out(bussplitter_3_d7));
  PullDown pulldown_53 (.out(bussplitter_3_d8));
  LED D7 (.in(d_ff_1_q[7]));
  LED A7 (.in(d_ff_2_q[7]));
  DipSwitch _7 (.out(_15_out[7]));
  ALU alu_1 (
    .Sum(alu_1_sum), .C_sel(\Σ_Csel ), .C_val(\Σ_Cval ), .nCin(FLAGS[3]), .A(OP1_q), .Sel(\Σ_sel ),
    .B(OP2_out), .M(\Σ_M ), .C_f(alu_1_c_f[3]), .N_f(alu_1_c_f[2]), .Z_f(alu_1_c_f[1]), .V_f(alu_1_c_f[0]));
  // _74245 _74245_3: pin names not known; wires that end beside it: REG_dir, 1'b1, 1'b0, bussplitter_3_d0, bussplitter_3_d1, bussplitter_3_d2, bussplitter_3_d3, bussplitter_3_d4, bussplitter_3_d5, bussplitter_3_d6, bussplitter_3_d7, 1'b0, _74245_3_p13, _74245_3_p14, _74245_3_p15, _74245_3_p16, _74245_3_p17, _74245_3_p18, _74245_3_p19, _74245_3_p20
  // _74245 _74245_4: pin names not known; wires that end beside it: REG_dir, 1'b1, 1'b0, bussplitter_3_d8, bussplitter_3_d9, bussplitter_3_d10, bussplitter_3_d11, bussplitter_3_d12, bussplitter_3_d13, bussplitter_3_d14, bussplitter_3_d15, 1'b0, _74245_4_p13, _74245_4_p14, _74245_4_p15, _74245_4_p16, _74245_4_p17, _74245_4_p18, _74245_4_p19, _74245_4_p20
  LED D5 (.in(d_ff_1_q[5]));
  LED D6 (.in(d_ff_1_q[6]));
  LED A5 (.in(d_ff_2_q[5]));
  LED A6 (.in(d_ff_2_q[6]));
  DipSwitch _5 (.out(_15_out[5]));
  DipSwitch _6 (.out(_15_out[6]));
  assign driverinvsel_3_out = ~nF_DATin ? DATA[3:0] : 4'bz;  // DriverInvSel driverinvsel_3
  LED D4 (.in(d_ff_1_q[4]));
  LED A4 (.in(d_ff_2_q[4]));
  DipSwitch _4 (.out(_15_out[4]));
  assign driverinvsel_3_out = ~nF_ALUin ? alu_1_c_f : 4'bz;  // DriverInvSel driverinvsel_4
  assign DATA = ~nRSH_DATout ? barrelshifter_1_out : 16'bz;  // DriverInvSel driverinvsel_5
  assign DATA = ~nSEX_DATout ? bitextender_1_out : 16'bz;  // DriverInvSel driverinvsel_6
  assign DATA = ~nSWP_DATout ? {OP1_q[7:0], OP1_q[15:8]} : 16'bz;  // DriverInvSel driverinvsel_7
  PullDown pulldown_54 (.out(_74245_4_p20));
  PullDown pulldown_55 (.out(_74245_4_p19));
  PullDown pulldown_56 (.out(_74245_4_p18));
  LED D3 (.in(d_ff_1_q[3]));
  and and_10 (and_10_out, CLK2, ~HLT_ack);  // And
  LED A3 (.in(d_ff_2_q[3]));
  and and_11 (and_11_out, CLK2, ~HLT_ack);  // And
  DipSwitch _3 (.out(_15_out[3]));
  PullDown #(.Bits(4)) pulldown_57 (.out(driverinvsel_3_out));
  PullDown #(.Bits(16)) pulldown_58 (.out(DATA));
  PullDown #(.Bits(16)) pulldown_59 (.out(DATA));
  PullDown #(.Bits(16)) pulldown_60 (.out(DATA));
  PullDown pulldown_61 (.out(_74245_4_p17));
  PullDown pulldown_62 (.out(_74245_4_p16));
  PullDown pulldown_63 (.out(_74245_4_p15));
  PullDown pulldown_64 (.out(_74245_4_p14));
  LED D1 (.in(d_ff_1_q[1]));
  LED D2 (.in(d_ff_1_q[2]));
  D_FF #(.Bits(16)) d_ff_1 (.D(DATA), .C(and_10_out), .Q(d_ff_1_q));  // open: nQ
  LED A1 (.in(d_ff_2_q[1]));
  LED A2 (.in(d_ff_2_q[2]));
  D_FF #(.Bits(16)) d_ff_2 (.D(ADDRESS), .C(and_11_out), .Q(d_ff_2_q));  // open: nQ
  DipSwitch _1 (.out(_15_out[1]));
  DipSwitch _2 (.out(_15_out[2]));
  Register #(.Bits(4)) F__NZVC (.D(driverinvsel_3_out), .C(CLK2), .en(~nF_st), .Q(FLAGS));
  PullDown pulldown_65 (.out(_74245_4_p13));
  PullDown pulldown_66 (.out(_74245_3_p20));
  PullDown pulldown_67 (.out(_74245_3_p19));
  PullDown pulldown_68 (.out(_74245_3_p18));
  LED D0 (.in(d_ff_1_q[0]));
  LED A0 (.in(d_ff_2_q[0]));
  assign DATA = ~1'b1 ? _15_out : 16'bz;  // DriverInvSel driverinvsel_8
  DipSwitch _0 (.out(_15_out[0]));
  PullDown pulldown_69 (.out(_74245_3_p17));
  PullDown pulldown_70 (.out(_74245_3_p16));
  PullDown pulldown_71 (.out(_74245_3_p15));
  PullDown pulldown_72 (.out(_74245_3_p14));
  not not_67 (not_67_out, REG_dir);
  BusSplitter #(.Bits(16)) bussplitter_4 (
    .D(DATA), .OE(not_67_out), .D0(_74245_3_p13), .D1(_74245_3_p14), .D2(_74245_3_p15), .D3(_74245_3_p16),
    .D4(_74245_3_p17), .D5(_74245_3_p18), .D6(_74245_3_p19), .D7(_74245_3_p20), .D8(_74245_4_p13),
    .D9(_74245_4_p14), .D10(_74245_4_p15), .D11(_74245_4_p16), .D12(_74245_4_p17), .D13(_74245_4_p18),
    .D14(_74245_4_p19), .D15(_74245_4_p20));
  PullDown pulldown_73 (.out(_74245_3_p13));
  LED V (.in(FLAG_V));
  LED C (.in(not_68_out));
  not not_68 (not_68_out, FLAG_C);
  assign HLT = ~nPAN_HLTen ? RUN_out : 1'bz;  // DriverInvSel driverinvsel_9
  DipSwitch RUN (.out(RUN_out));
  assign DATA = ~nSUM_DATout ? alu_1_sum : 16'bz;  // DriverInvSel driverinvsel_10
  PullDown #(.Bits(16)) pulldown_74 (.out(DATA));
  assign DATA = ~nF_DATout ? {{5{1'b0}}, undriven, FLAGS} : 16'bz;  // DriverInvSel driverinvsel_11
  PullDown #(.Bits(16)) pulldown_75 (.out(DATA));
  LED Z (.in(FLAGS[1]));
  DipSwitch STEP (.out(STP));
  LED N (.in(FLAGS[0]));
  CounterPreset #(.Bits(16)) PC (
    .en(~nPC_en), .C(CLK2), .dir(1'b0), .in(DATA), .ld(~nPC_st), .clr(1'b0), .out(PC_out));  // open: ovf
  CounterPreset #(.Bits(16)) SP (
    .en(~nSP_en), .C(CLK2), .dir(SP_dir), .in(DATA), .ld(~nSP_st), .clr(1'b0), .out(SP_out));  // open: ovf
  assign ADDRESS = ~nPC_ADSout ? PC_out : 16'bz;  // DriverInvSel driverinvsel_12
  assign ADDRESS = ~nSP_ADSout ? SP_out : 16'bz;  // DriverInvSel driverinvsel_13
  assign DATA = ~nPC_DATout ? PC_out : 16'bz;  // DriverInvSel driverinvsel_14
  PullDown #(.Bits(16)) pulldown_76 (.out(DATA));
  PullDown #(.Bits(16)) pulldown_77 (.out(ADDRESS));
  assign DATA = ~nSP_DATout ? SP_out : 16'bz;  // DriverInvSel driverinvsel_15
  PullDown #(.Bits(16)) pulldown_78 (.out(DATA));
  PullDown #(.Bits(16)) pulldown_79 (.out(ADDRESS));
  not not_69 (not_69_out, STP);
  Register #(.Bits(16)) MDR (.D(DATA), .C(CLK2), .en(~nMDR_st), .Q(MDR_q));
  Register MAR (.D(DATA[0]), .C(CLK2), .en(nMAR_st), .Q(MAR_q[0]));
  // _7474 _7474_2: pin names not known; wires that end beside it: not_69_out, 1'b0, 1'b0, HLT_ack, 1'b0, 1'b0, 1'b0, 1'b0, 1'b1, 1'b0, nPAN_HLTen
  assign DATA = ~nMDR_DATout ? MDR_q : 16'bz;  // DriverInvSel driverinvsel_16
  assign ADDRESS = ~nMAR_ADSout ? MAR_q : 16'bz;  // DriverInvSel driverinvsel_17
  PullDown #(.Bits(16)) pulldown_80 (.out(DATA));
  PullDown #(.Bits(16)) pulldown_81 (.out(ADDRESS));
  // Pins of 2 and 4 bits meet at FLAGS
  // Pins of 1 and 16 bits meet at DATA
  // Pins of 1 and 16 bits meet at MAR_q

  // Other names for the same wires on the sheet: CLK_1 = CLK1; CLK_2 = CLK2

  // Notes on the sheet:
  //   Clock: Hz: 50
  //   Control Sequencing
  //   Control Decoding
  //   Memory/IRQ
  //   contents of ROM_16x64k (hex, n*v repeats v):
  //   57328*0,16*25,13c0,48,b350,8188*0,e000
  //   contents of µCODE (hex, n*v repeats v):
  //   49820002a5,2002801,2000082,1820002a6,20004000092,11*0,16*8800000000
  //   ,49820002a5,14000008,14*0,16*8800000000,49820002a5,12000000,14*0
  //   ,16*8800000000,49820002a5,14000008,14*0,16*8800000000,49820002a5
  //   ,12000000,14*0,48*8800000000,49820002a5,12000000,14*0,16*8800000000
  //   ,49820002a5,14000008,14*0,16*8800000000,49820002a5,14000000,14*0
  //   ,16*8800000000,49820002a5,14000008,14*0,16*8800000000,49820002a5
  //   ,14000000,14*0,16*8800000000,49820002a5,14000008,14*0,16*8800000000
  //   ,49820002a5,14000000,14*0,16*8800000000,49820002a5,14000008,14*0
  //   ,16*8800000000,49820002a5,12000000,14*0,16*8800000000,49820002a5
  //   ,14000008,14*0,16*8800000000,49820002a5,14000008,14*0,16*8800000000
  //   ,49820002a5,14000008,14*0,16*8800000000,49820002a5,12000000,801820002a8
  //   ,94000307,12*0,16*8800000000,49820002a5,14000008,14*0,16*8800000000
  //   ,49820002a5,2000034,12000000,1820002a3,80013240048,84000307,10*0
  //   ,16*8800000000,49820002a5,14000008,14*0,16*8800000000,49820002a5
  //   ,800120000b8,84000307,13*0,16*8800000000,49820002a5,14000008,14*0
  //   ,16*8800000000,49820002a5,120000b4,1820002a3,80013240048,84000307
  //   ,11*0,16*8800000000,49820002a5,14000008,14*0,16*8800000000,49820002a5
  //   ,800120000bb,82000307,53c0048,12*0,16*8800000000,49820002a5,14000008
  //   ,14*0,16*8800000000,49820002a5,120000b3,80002000048,84000307,12*0
  //   ,16*8800000000,49820002a5,14000008,14*0,16*8800000000,49820002a5
  //   ,14000000,14*0,16*8800000000,49820002a5,14000008,14*0,16*8800000000
  //   ,49820002a5,14000000,14*0,16*8800000000,49820002a5,14000008,14*0
  //   ,16*8800000000,49820002a5,12000000,1820002a6,4000092,12*0,16*8800000000
  //   ,49820002a5,14000008,14*0,16*8800000000,49820002a5,2000034,12000000
  //   ,1820002a3,5240042,11*0,16*8800000000,49820002a5,14000008,14*0
  //   ,16*8800000000,49820002a5,40000b2,14*0,16*8800000000,49820002a5
  //   ,14000008,14*0,16*8800000000,49820002a5,120000b4,1820002a3,5240042
  //   ,12*0,16*8800000000,49820002a5,14000008,14*0,16*8800000000,49820002a5
  //   ,20000b3,53c0048,13*0,16*8800000000,49820002a5,14000008,14*0,16*8800000000
  //   ,49820002a5,20000b3,2000048,40000b2,12*0,16*8800000000,49820002a5
  //   ,14000008,14*0,16*8800000000,49820002a5,14000000,14*0,16*8800000000
  //   ,49820002a5,14000008,14*0,16*8800000000,49820002a5,12000000,14*0
  //   ,16*8800000000,49820002a5,14000008,14*0,16*8800000000,49820002a5
  //   ,12000000,14*0,16*8800000000,49820002a5,14000008,14*0,16*8800000000
  //   ,49820002a5,12000000,14*0,16*8800000000,49820002a5,14000008,14*0
  //   ,16*8800000000,49820002a5,12000000,14*0,16*8800000000,49820002a5
  //   ,14000008,14*0,16*8800000000,49820002a5,12000000,14*0,16*8800000000
  //   ,49820002a5,14000008,14*0,16*8800000000,49820002a5,12000000,14*0
  //   ,16*8800000000,49820002a5,14000008,14*0,16*8800000000,49820002a5
  //   ,12000000,14*0,16*8800000000,49820002a5,14000008,14*0,16*8800000000
  //   ,49820002a5,12000000,14*0,16*8800000000,49820002a5,14000008,14*0
  //   ,16*8800000000,49820002a5,12000000,14*0,16*8800000000,49820002a5
  //   ,14000008,14*0,16*8800000000,49820002a5,12000000,14*0,16*8800000000
  //   ,49820002a5,14000008,14*0,16*8800000000,49820002a5,12000000,14*0
  //   ,16*8800000000,49820002a5,14000008,14*0,16*8800000000,49820002a5
  //   ,12000000,14*0,16*8800000000,49820002a5,14000008,14*0,16*8800000000
  //   ,49820002a5,12000000,14*0,16*8800000000,49820002a5,14000008,14*0
  //   ,16*8800000000,49820002a5,12000000,14*0,16*8800000000,49820002a5
  //   ,14000008,14*0,16*8800000000,49820002a5,12000000,14*0,16*8800000000
  //   ,49820002a5,14000008,14*0,16*8800000000,49820002a5,12000000,14*0
  //   ,16*8800000000,49820002a5,14000008,14*0,16*8800000000,49820002a5
  //   ,12000000,14*0,16*8800000000,49820002a5,14000008,14*0,16*8800000000
  //   ,49820002a5,12000000,14*0,16*8800000000,49820002a5,14000008,14*0
  //   ,16*8800000000,49820002a5,12000000,14*0,16*8800000000,49820002a5
  //   ,14000008,14*0,16*8800000000,49820002a5,12000000,14*0,16*8800000000
  //   ,49820002a5,14000008,14*0,16*8800000000,49820002a5,12000000,14*0
  //   ,16*8800000000,49820002a5,14000008,14*0,16*8800000000,49820002a5
  //   ,12000000,14*0,16*8800000000,49820002a5,14000008,14*0,16*8800000000
  //   ,49820002a5,12000000,14*0,16*8800000000,49820002a5,14000008,14*0
  //   ,16*8800000000,49820002a5,12000000,14*0,16*8800000000,49820002a5
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  //   ALU
  //   Registers
  //   Control Panel
  //   ATLAS CPU-16
  //   By Hayden B.
endmodule
