// Digital circuit CPU 4.dig as structural Verilog
module CPU_4 (
);

  wire _74181_1_p17, _74181_1_p18, _74245_1_p13, _74245_1_p14, _74245_1_p15, _74245_1_p16, ALU_DATout, B_st,
       bussplitter_1_d0, bussplitter_1_d1, bussplitter_1_d2, bussplitter_1_d3, C_st, CLK_2,
       demultiplexer_1_out_0, demultiplexer_1_out_1, demultiplexer_2_out_0, demultiplexer_2_out_1,
       demultiplexer_3_out_1, demultiplexer_3_out_2, demultiplexer_3_out_3, demultiplexer_3_out_4,
       demultiplexer_3_out_5, demultiplexer_3_out_6, demultiplexer_3_out_7, demultiplexer_4_out_0,
       demultiplexer_4_out_1, demultiplexer_4_out_2, demultiplexer_4_out_3, demultiplexer_5_out_1,
       demultiplexer_5_out_2, demultiplexer_5_out_3, MAR_ADSout, MARH_st, MARL_st, MEM_DATout, MEM_dir,
       MEM_en, MEM_st, nMEM_DATout, nMEM_st, not_1_out, not_2_out, not_3_out, not_4_out, not_5_out,
       nPC_ADSout, nPC_DATout, nPC_en, nPC_st, OP1_st, OP2_st, OPS_st, PC_st, RAR_st, REG_DATout, REG_st;
  wire [2:0] DOUT_SEL, DOUT_sel_t;
  wire [3:0] _74181_1_p9, _74181_1_p13, MARH_q, MARL_q, multiplexer_1_out, multiplexer_2_out, OP1_q, OP2_q,
       RAR_q, REG__16x4_d, ST_sel;
  wire [15:0] ADDRESS, DATA, MEMDATA_in, PC_out;
  wire [15:7] rom_1_d;

  Demultiplexer demultiplexer_1 (
    .sel(ADDRESS[7]), .in(not_1_out), .out_0(demultiplexer_1_out_0), .out_1(demultiplexer_1_out_1));
  not not_1 (not_1_out, MEM_en);
  not not_2 (not_2_out, demultiplexer_1_out_0);
  not not_3 (not_3_out, demultiplexer_1_out_1);
  ROM #(.AddrBits(8), .Bits(4)) ROM_16x64k (.A(ADDRESS[7:0]), .sel(not_4_out), .D(MEMDATA_in[3:0]));
  not not_4 (not_4_out, not_2_out);
  RAMSinglePortSel #(.AddrBits(8), .Bits(4)) RAM0_16x64k (
    .A(ADDRESS[7:0]), .CS(~not_3_out), .WE(~nMEM_st), .OE(~nMEM_DATout), .D(MEMDATA_in[3:0]));
  BusSplitter #(.Bits(4)) bussplitter_1 (
    .D(MEMDATA_in[3:0]), .OE(MEM_dir), .D0(bussplitter_1_d0), .D1(bussplitter_1_d1), .D2(bussplitter_1_d2),
    .D3(bussplitter_1_d3));
  PullDown #(.Bits(16)) pulldown_1 (.out(MEMDATA_in));
  PullDown pulldown_2 (.out(bussplitter_1_d0));
  PullDown pulldown_3 (.out(bussplitter_1_d1));
  PullDown pulldown_4 (.out(bussplitter_1_d2));
  // _74245 _74245_1: pin names not known; wires that end beside it: MEM_dir, 1'b1, 1'b0, bussplitter_1_d0, bussplitter_1_d1, bussplitter_1_d2, bussplitter_1_d3, 1'b0, 1'b0, 1'b0, 1'b0, MEM_en, _74245_1_p13, _74245_1_p14, _74245_1_p15, _74245_1_p16, 1'b0, 1'b0, 1'b0, 1'b0
  PullDown pulldown_5 (.out(bussplitter_1_d3));
  PullDown pulldown_6 (.out(_74245_1_p16));
  PullDown pulldown_7 (.out(_74245_1_p15));
  PullDown pulldown_8 (.out(_74245_1_p14));
  PullDown pulldown_9 (.out(_74245_1_p13));
  BusSplitter #(.Bits(4)) bussplitter_2 (
    .D(DATA[3:0]), .OE(not_5_out), .D0(_74245_1_p13), .D1(_74245_1_p14), .D2(_74245_1_p15), .D3(_74245_1_p16));
  not not_5 (not_5_out, MEM_dir);
  ROM #(.Bits(16)) rom_1 (.D({rom_1_d, DOUT_sel_t, ST_sel}));  // open: A, sel
  Demultiplexer demultiplexer_2 (
    .sel(ST_sel[3]), .in(1'b1), .out_0(demultiplexer_2_out_0), .out_1(demultiplexer_2_out_1));
  Register #(.Bits(4)) OP1 (.D(DATA[3:0]), .Q(OP1_q));  // open: C, en
  Register #(.Bits(4)) OP2 (.D(DATA[3:0]), .Q(OP2_q));  // open: C, en
  assign DATA[3:0] = ~ALU_DATout ? _74181_1_p9 : 4'bz;  // DriverInvSel driverinvsel_1
  PullDown #(.Bits(4)) pulldown_10 (.out(DATA[3:0]));
  Demultiplexer #(.Selector_Bits(3)) demultiplexer_3 (
    .sel(ST_sel[2:0]), .in(demultiplexer_2_out_0), .out_1(demultiplexer_3_out_1),
    .out_2(demultiplexer_3_out_2), .out_3(demultiplexer_3_out_3), .out_4(demultiplexer_3_out_4),
    .out_5(demultiplexer_3_out_5), .out_6(demultiplexer_3_out_6), .out_7(demultiplexer_3_out_7));  // open: out_0
  Demultiplexer #(.Selector_Bits(3)) demultiplexer_4 (
    .sel(ST_sel[2:0]), .in(demultiplexer_2_out_1), .out_0(demultiplexer_4_out_0),
    .out_1(demultiplexer_4_out_1), .out_2(demultiplexer_4_out_2), .out_3(demultiplexer_4_out_3));  // open: out_4, out_5, out_6, out_7
  not not_6 (OP1_st, demultiplexer_3_out_1);
  not not_7 (OP2_st, demultiplexer_3_out_2);
  not not_8 (OPS_st, demultiplexer_3_out_3);
  not not_9 (REG_st, demultiplexer_3_out_4);
  not not_10 (B_st, demultiplexer_3_out_5);
  not not_11 (C_st, demultiplexer_3_out_6);
  not not_12 (PC_st, demultiplexer_3_out_7);
  not not_13 (MEM_st, demultiplexer_4_out_0);
  not not_14 (MARL_st, demultiplexer_4_out_1);
  not not_15 (MARH_st, demultiplexer_4_out_2);
  not not_16 (RAR_st, demultiplexer_4_out_3);
  Register #(.Bits(4)) RAR (.D(DATA[3:0]), .Q(RAR_q));  // open: C, en
  Demultiplexer #(.Selector_Bits(3)) demultiplexer_5 (
    .sel(DOUT_SEL), .in(1'b1), .out_1(demultiplexer_5_out_1), .out_2(demultiplexer_5_out_2),
    .out_3(demultiplexer_5_out_3));  // open: out_0, out_4, out_5, out_6, out_7
  // _74181 _74181_1: pin names not known; wires that end beside it: OP1_q[0], OP1_q[1], OP1_q[2], OP1_q[3], OP2_q[0], OP2_q[1], OP2_q[2], OP2_q[3], _74181_1_p9[0], _74181_1_p9[1], _74181_1_p9[2], _74181_1_p9[3], _74181_1_p13[0], _74181_1_p13[1], _74181_1_p13[2], _74181_1_p13[3], _74181_1_p17, _74181_1_p18
  CounterPreset #(.Bits(16)) PC (
    .en(~nPC_en), .C(CLK_2), .dir(1'b0), .in(DATA), .ld(~nPC_st), .clr(1'b0), .out(PC_out));  // open: ovf
  Register #(.Bits(4)) MARL (.D(DATA[3:0]), .Q(MARL_q));  // open: C, en
  Register #(.Bits(4)) MARH (.D(DATA[3:0]), .Q(MARH_q));  // open: C, en
  RAMDualPort #(.AddrBits(4), .Bits(4)) REG__16x4 (.A(RAR_q), .Din(DATA[3:0]), .D(REG__16x4_d));  // open: str, C, ld
  not not_17 (REG_DATout, demultiplexer_5_out_1);
  not not_18 (ALU_DATout, demultiplexer_5_out_2);
  not not_19 (MEM_DATout, demultiplexer_5_out_3);
  assign ADDRESS = ~nPC_ADSout ? PC_out : 16'bz;  // DriverInvSel driverinvsel_2
  assign DATA = ~nPC_DATout ? PC_out : 16'bz;  // DriverInvSel driverinvsel_3
  assign ADDRESS[3:0] = ~MAR_ADSout ? MARL_q : 4'bz;  // DriverInvSel driverinvsel_4
  assign ADDRESS[3:0] = ~MAR_ADSout ? MARH_q : 4'bz;  // DriverInvSel driverinvsel_5
  assign DATA[3:0] = ~REG_DATout ? REG__16x4_d : 4'bz;  // DriverInvSel driverinvsel_6
  Register #(.Bits(4)) OPS (.D(DATA[3:0]), .Q(_74181_1_p13));  // open: C, en
  PullDown #(.Bits(16)) pulldown_11 (.out(DATA));
  PullDown #(.Bits(16)) pulldown_12 (.out(ADDRESS));
  PullDown #(.Bits(4)) pulldown_13 (.out(ADDRESS[3:0]));
  PullDown #(.Bits(4)) pulldown_14 (.out(ADDRESS[3:0]));
  PullDown #(.Bits(4)) pulldown_15 (.out(DATA[3:0]));
  Multiplexer multiplexer_1 (.in_0(_74181_1_p17), .in_1(DATA[0]), .out(multiplexer_1_out[0]));  // open: sel
  Multiplexer multiplexer_2 (.in_0(_74181_1_p18), .in_1(DATA[0]), .out(multiplexer_2_out[0]));  // open: sel
  Register #(.Bits(4)) E (.D(multiplexer_1_out));  // open: C, en, Q
  Register #(.Bits(4)) C (.D(multiplexer_2_out));  // open: C, en, Q
  // Pins of 1 and 4 and 16 bits meet at DATA
  // Pins of 3 and 4 bits meet at ST_sel
  // Pins of 1 and 4 bits meet at multiplexer_1_out
  // Pins of 1 and 4 bits meet at multiplexer_2_out
  // Pins of 4 and 8 and 16 bits meet at ADDRESS
  // Pins of 4 and 16 bits meet at MEMDATA_in

  // Notes on the sheet:
  //   contents of ROM_16x64k (hex, n*v repeats v):
  //   56006*0,5,1321*0,16*45,40,48,4d,dea8,40,45,4d,dea8,40,4c,4d,dea8
  //   ,40,4c,4d,dea8,40,4f,4d,dea8,40,2c,4d,dea8,40,20,4d,dea8,40,57
  //   ,4d,dea8,40,4f,4d,dea8,40,52,4d,dea8,40,4c,4d,dea8,40,44,4d,dea8
  //   ,40,21,4d,dea8,1,8138*0,e000
endmodule
